# Fritzing sketch PushThru ESP8266 Fritzing PCB (saved by Fritzing 0.9.3b)
circuit board: 5.09763cm x 2.30011cm
breadboards: 1

parts:
  1M = Resistor [tolerance=±5% resistance=1M package=THT]
  180Ω = Resistor [tolerance=±5% resistance=180 package=THT]
  220k = Resistor [tolerance=±5% resistance=220k package=THT]
  12k = Resistor [tolerance=±5% resistance=12k package=THT]
  RGB_LED = RGB LED (com. cathode, rbg) [package="5 mm [THT]"]
  Momentary_Switch1 = SWITCH-MOMENTARY-2 [package=tactile-pth-12mm]

nets:
  N1: 1M.Pin_0, 220k.Pin_0
  N2: 180Ω.Pin_0, 220k.Pin_1, Momentary_Switch1.1
  N3: 180Ω.Pin_1, RGB_LED.common_cathode
  N4: 12k.Pin_1, Momentary_Switch1.3

notes:
  +
  BUTTON
  V1.0
  BUZZER
  R1
  R2
  R3
  R4

custom parts:
  SWITCH-MOMENTARY-2: Various NO switches- pushbuttons, reed, etc
