# Fritzing sketch PushThru ESP8266 Fritzing Schematic (saved by Fritzing 0.9.3b)

parts:
  With_Protoboard = Adafruit Feather HUZZAH ESP8266 [part_number="RS 124-5505 & 124-5515"]
  Momentary_Switch = Momentary Switch [part_number="RS 123-9632 + RS 123-9569" package=ksa_sealed_tac_switch]
  R2 = Resistor [tolerance=±5% resistance=12k part_number="RS 707-7757" package=THT]
  R1 = Resistor [tolerance=±5% resistance=180 part_number="RS 131-160" package=THT]
  Buzzer = Piezo Speaker [part_number="RS 535-8253"]
  LED = RGB LED (com. cathode, rbg) [part_number="RS 861-4307" package="5 mm [THT]"]
  R3 = Resistor [tolerance=±0.1% resistance=1M part_number="RS 754-8770" package=THT]
  R4 = Resistor [tolerance=±1% resistance=220k part_number="RS 683-3310" package=THT]

nets:
  N1: With_Protoboard.GPIO12/MISO, LED.red_anode
  N2: With_Protoboard.GPIO13/MOSI, LED.blue_anode
  N3: With_Protoboard.ADC, R3.Pin_0, R4.Pin_0
  N4: With_Protoboard.GND, Momentary_Switch.2, R1.Pin_1, Buzzer.pin2, R4.Pin_1
  N5: With_Protoboard.3.3V, R2.Pin_1
  N6: With_Protoboard.RESET, With_Protoboard.GPIO16, Momentary_Switch.4
  N7: With_Protoboard.VBAT, R3.Pin_1
  N8: With_Protoboard.GPIO14/SCK, LED.green_anode
  N9: With_Protoboard.GPIO15, Buzzer.pin1
  N10: Momentary_Switch.3, R2.Pin_0
  N11: R1.Pin_0, LED.common_cathode

notes:
  Pantri: A Bit Pushy
  PB01
  All components should be installed on Adafruit Feather Proto Board & connected to Feather Huzzah using the standard pins that come with the two boards.
  This schematic is shared under the GNU General Public License v3.0.
  www.pantri.net
  github.com/pantri/A-Bit-Pushy

custom parts:
  Adafruit Feather HUZZAH ESP8266: his is the Adafruit Feather HUZZAH ESP8266 - our take on an 'all-in-one' ESP8266 WiFi development board with built in USB and battery charging. Its an ESP8266 WiFi module with all the extras you need, ready to rock! We have other boards in the Feather family, check'em out here. At the Feather HUZZAH's heart is an ESP8266 WiFi microcontroller clocked at 80 MHz and at 3.3V logic. This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
